# Fritzing sketch 51300239ce395f4032000001 (saved by Fritzing 0.7.11b)

parts:
  Part1 = Wake-On-Shake Board
  Part3 = Mono Audio Amp Breakout
  Part5 = Power Cell - LiPo Charger/Booster
  Part4 = Arduino Pro Mini 3.3V
  Part2 = Parallax emic2 Text-To-Speech
  J1 = Piezo Speaker

nets:
  VIN: Part1.VIN, Part5.5V
  N1: Part1.GND#22, Part5.GND
  N2: Part1.WAKE, Part4.D9
  VIN_2: Part1.VOUT, Part3.VIN, Part4.VCC, Part2.5V
  GND: Part1.GND#30, Part3.GND, Part4.GND, Part2.GND
  N3: Part3.IN+, Part2.SP+
  N4: Part3.IN-, Part2.SP-
  N5: Part3.OUT+, J1.pin2
  N6: Part3.OUT-, J1.pin1
  N7: Part4.D3, Part2.SIN
  N8: Part4.D2, Part2.SOUT

custom parts:
  Mono Audio Amp Breakout: Description: This tiny audio amplifier is based on the Texas Instruments TPA2005D1. Its efficient class-D operation means low heat and long battery life. It can drive an 8-Ohm speaker at up to 1.4 Watts; it won't shake a stadium, but it will provide plenty of volume for your audio projects. The fully-differential inputs are safe for floating audio signals such as from our MP3 Shield, and can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
  Power Cell - LiPo Charger/Booster: Description: The PowerCell board is a single cell LiPo boost converter (to 3.3V and 5V) and micro-USB charger in one. The board comes with a JST connector for a single cell LiPo battery, a micro-USB connector for the 5V charge input, and selectable 3.3V and 5V ouput pins (labeled 'out'). There are also two charge pins broken out (labeled 'charge'), so you can use another 5V power source to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
  Parallax emic2 Text-To-Speech: Give your project a voice! Designed in conjunction with Grand Idea Studio, the Emic 2 Text-to-Speech Module is a multi-language voice synthesizer that converts a stream of digital text into natural sounding speech. Its simple command-based interface makes it easy to integrate into any embedded system. Key Features: High-quality speech synthesis for English and Spanish languages Nine pre-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
