# Fritzing sketch Push To Play (saved by Fritzing 0.9.3b)
breadboards: 2

parts:
  Mono_Amplifier = Mono Audio Amp Breakout
  SparkFun_MP3_Player_Shield = Arduino MP3 Player Shield
  SparkFun_RedBoard = Arduino Uno (Rev3) - ICSP  # not connected
  Triple_Axis_Accelerometer = Triple Axis Accelerometer Breakout - ADXL335
  Rotary_Potentiometer = Rotary Potentiometer (Small) [maximum_resistance=100kΩ package=THT]
  Speaker = SPEAKER [package=pcb_mount_speaker]  # not connected
  Force_Senstive_Resistor = Basic Force Sensing Resistor (FSR) [package=THT]
  R3 = Resistor [tolerance=±5% resistance=100 package="2512 [SMD]"]
  U1 = LIPO-2000mAh [package=lipo-2000]
  Part2 = sparkfun-battery-babysitter
  Part3 = Arduino Pro Mini v13

nets:
  N1: Mono_Amplifier.IN+, SparkFun_MP3_Player_Shield.RIGHT
  N2: Mono_Amplifier.IN-, SparkFun_MP3_Player_Shield.GBUF
  VIN: Mono_Amplifier.VIN, SparkFun_MP3_Player_Shield.3.3, Triple_Axis_Accelerometer.VCC
  GND: Mono_Amplifier.GND, SparkFun_MP3_Player_Shield.GND, Triple_Axis_Accelerometer.GND, R3.Pin_1, U1.-, Part2.GND, Part3.GND
  N3: Mono_Amplifier.VOL+, Rotary_Potentiometer.leg1
  N4: Mono_Amplifier.VOL-, Rotary_Potentiometer.leg2
  N5: Mono_Amplifier.VOL, Rotary_Potentiometer.wiper
  N6: SparkFun_MP3_Player_Shield.VCC, Force_Senstive_Resistor.pin_0
  N7: SparkFun_MP3_Player_Shield.A0, Triple_Axis_Accelerometer.XOUT
  N8: SparkFun_MP3_Player_Shield.A1, Triple_Axis_Accelerometer.YOUT
  N9: SparkFun_MP3_Player_Shield.A2, Triple_Axis_Accelerometer.ZOUT
  N10: SparkFun_MP3_Player_Shield.A3, Force_Senstive_Resistor.pin_1, R3.Pin_0
  N11: SparkFun_MP3_Player_Shield.VIN, Part2.OUT, Part3.RAW
  N12: U1.+, Part2.BATTERY_IN
  N13: Part2.V_PU, Part3.VCC
  N14: Part2.SDA, Part3.A4
  N15: Part2.SCL, Part3.A5

custom parts:
  Mono Audio Amp Breakout: Description: This tiny audio amplifier is based on the Texas Instruments TPA2005D1. Its efficient class-D operation means low heat and long battery life. It can drive an 8-Ohm speaker at up to 1.4 Watts; it won't shake a stadium, but it will provide plenty of volume for your audio projects. The fully-differential inputs are safe for floating audio signals such as from our MP3 Shield, and can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
